// Logisim project Pipelined Processor Design.circ as structural Verilog: 3 circuits, main circuit main
module main (
);

  wire and_1_out, and_7_out, and_8_out, Clk, comparator_1_gt, decoder_1_out1, decoder_1_out2, decoder_1_out4,
       decoder_1_out6, not_1_out, not_2_out, not_3_out, not_4_out, not_5_out, or_4_out;
  wire [0:0] decoder_1_out5, undriven_2;
  wire [2:0] Func, J_Type, or_3_out, undriven_3;
  wire [3:0] OpCode;
  wire [5:0] decoder_1_out7;
  wire [11:0] adder_1_out, bit_extender_1_out, multiplexer_1_out, PC_q, SevenPC, undriven;
  wire [11:3] J;
  wire [15:0] alu_1_rd, registerfile_1_busa, registerfile_1_busb;

  Clock clock_1 (.out(Clk));
  and and_1 (and_1_out, decoder_1_out7[5], undriven_2[0]);
  and and_2 (and_1_out, decoder_1_out7[4], undriven_2[0]);
  and and_3 (and_1_out, decoder_1_out7[3], undriven_2[0]);
  assign bit_extender_1_out = {{6{J[5]}}, {J[5:3], Func}};  // Bit_Extender bit_extender_1
  and and_4 (and_1_out, decoder_1_out7[2], undriven_2[0]);
  and and_5 (and_1_out, decoder_1_out7[1], undriven_2[0]);
  Adder #(.width(12)) adder_1 (.a(PC_q), .b(bit_extender_1_out), .out(adder_1_out));  // open: cin, cout
  and and_6 (and_1_out, decoder_1_out7[0], undriven_2[0]);
  and and_7 (and_7_out, decoder_1_out1, not_1_out, not_3_out, not_2_out, Func[2], Func[1], Func[0]);
  not not_1 (not_1_out, undriven_3[2]);
  not not_2 (not_2_out, undriven_3[0]);
  not not_3 (not_3_out, undriven_3[1]);
  and and_8 (and_8_out, decoder_1_out1, Func[2], Func[1], not_4_out);
  not not_4 (not_4_out, Func[0]);
  Adder #(.width(12)) adder_2 (.a(PC_q), .b(12'h1), .out(SevenPC));  // open: cin, cout
  or or_1 (or_3_out[2], J_Type[2], J_Type[1]);
  or or_2 (or_3_out[1], and_1_out, and_8_out);
  or or_3 (or_3_out[0], and_1_out, J_Type[2], and_8_out);
  Multiplexer #(.select(3), .width(12), .enable("false")) multiplexer_1 (
    .in0(SevenPC), .in1(undriven), .in2(undriven), .in3(adder_1_out), .in4({J, Func}), .in5({J, Func}),
    .in6(SevenPC), .in7(SevenPC), .out(multiplexer_1_out), .sel(or_3_out));
  Register #(.width(12)) PC (.D(multiplexer_1_out), .en(1'b1), .Q(PC_q), .clk(Clk));  // open: clr
  Decoder #(.select(4), .enable("false")) decoder_1 (
    .out1(decoder_1_out1), .out2(decoder_1_out2), .out3(decoder_1_out2), .out4(decoder_1_out4),
    .out5(decoder_1_out5[0]), .out6(decoder_1_out6), .out7(decoder_1_out7[0]), .out8(decoder_1_out7[1]),
    .out9(decoder_1_out7[2]), .out10(decoder_1_out7[3]), .out11(decoder_1_out7[4]),
    .out12(decoder_1_out7[5]), .out13(J_Type[0]), .out14(J_Type[1]), .out15(J_Type[2]), .sel(OpCode));  // open: out0
  or or_4 (or_4_out, and_8_out, not_5_out);
  not not_5 (not_5_out, comparator_1_gt);
  Comparator #(.width(11), .mode("unsigned")) comparator_1 (
    .a({J_Type[2:1], 1'b0, decoder_1_out7, 1'b0, decoder_1_out5[0]}), .b({11{1'b0}}), .gt(comparator_1_gt));  // open: eq, lt
  RAM #(.addrWidth(12), .dataWidth(16)) ram_1 (.addr(PC_q), .data({OpCode, J, Func}));  // open: sel, clk, ld, clr
  Bit_Extender #(.in_width(6), .\type ("sign")) bit_extender_2 (.in({J[5:3], Func}));  // open: out
  Bit_Extender #(.in_width(6)) bit_extender_3 (.in({J[5:3], Func}));  // open: out
  RegisterFile registerfile_1 (
    .Clock(Clk), .RegWrite(or_4_out), .RA(J[8:6]), .RB(J[5:3]), .RW(J[11:9]), .BusA(registerfile_1_busa),
    .BusB(registerfile_1_busb));  // open: BusW
  // OR_Gate or_5 has open pins: in0=decoder_1_out4, in1=decoder_1_out5[0], in2=decoder_1_out2, in3=decoder_1_out6, out=open
  // OR_Gate or_6 has open pins: in0=decoder_1_out5[0], in1=decoder_1_out6, out=open
  ALU alu_1 (.Op(OpCode), .func(Func), .Rt(registerfile_1_busa), .Rs(registerfile_1_busb), .Rd(alu_1_rd));
  RAM #(.addrWidth(16), .dataWidth(16), .bus("separate")) ram_2 (
    .str(decoder_1_out5[0]), .clk(Clk), .ld(decoder_1_out6));  // open: addr, din, data, sel, clr

  // Other names for the same wires on the sheet: J[2:0] = Func; Rt[2:0] = J[5:3]; Rs[2:0] = J[8:6]; Rd[2:0] = J[11:9];
  //   JAL = J_Type[2]

  // Notes on the sheet:
  //   JALR
  //   JR
  //   func
  //   Control Unit
  //   Branching Mux
  //   RegWrite
  //   R-type
  //   Instructions Memory
  //   I-Type
  //   Signed Or Zero
  //   SW
  //   LW
  //   BNE
  //   BEQ
  //   BGT
  //   BGE
  //   BLT
  //   BLE
  //   Jump
  //   Jump and Link
  //   J-type
  //   Load Upper Immediate
  //   ALUSrc
  //   DataMemory
endmodule

module RegisterFile (
  input  [15:0] BusW,
  input  [2:0] RB,
  input  [2:0] RA,
  input  Clock,
  input  RegWrite,
  input  [2:0] RW,
  output [15:0] BusB,
  output [15:0] BusA
);

  wire _1_out, _2_out, _3_out, _4_out, _5_out, _6_out, _7_out, decoder_1_out1, decoder_1_out2,
       decoder_1_out3, decoder_1_out4, decoder_1_out5, decoder_1_out6, decoder_1_out7, decoder_2_out0,
       decoder_2_out1, decoder_2_out2, decoder_2_out3, decoder_2_out4, decoder_2_out5, decoder_2_out6,
       decoder_2_out7, decoder_3_out0, decoder_3_out1, decoder_3_out2, decoder_3_out3, decoder_3_out4,
       decoder_3_out5, decoder_3_out6, decoder_3_out7;
  wire [15:0] R1_q, R2_q, R3_q, R4_q, R5_q, R6_q, R7_q;

  Decoder #(.select(3)) decoder_1 (
    .out1(decoder_1_out1), .out2(decoder_1_out2), .out3(decoder_1_out3), .out4(decoder_1_out4),
    .out5(decoder_1_out5), .out6(decoder_1_out6), .out7(decoder_1_out7), .sel(RW), .en(1'b1));  // open: out0
  and _1 (_1_out, decoder_1_out1, RegWrite);
  and _2 (_2_out, decoder_1_out2, RegWrite);
  and _3 (_3_out, decoder_1_out3, RegWrite);
  and _4 (_4_out, decoder_1_out4, RegWrite);
  and _5 (_5_out, decoder_1_out5, RegWrite);
  and _6 (_6_out, decoder_1_out6, RegWrite);
  and _7 (_7_out, decoder_1_out7, RegWrite);
  Register #(.width(16)) R1 (.D(BusW), .en(_1_out), .Q(R1_q), .clk(Clock));  // open: clr
  Register #(.width(16)) R2 (.D(BusW), .en(_2_out), .Q(R2_q), .clk(Clock));  // open: clr
  Register #(.width(16)) R3 (.D(BusW), .en(_3_out), .Q(R3_q), .clk(Clock));  // open: clr
  Register #(.width(16)) R4 (.D(BusW), .en(_4_out), .Q(R4_q), .clk(Clock));  // open: clr
  Register #(.width(16)) R5 (.D(BusW), .en(_5_out), .Q(R5_q), .clk(Clock));  // open: clr
  Register #(.width(16)) R6 (.D(BusW), .en(_6_out), .Q(R6_q), .clk(Clock));  // open: clr
  Register #(.width(16)) R7 (.D(BusW), .en(_7_out), .Q(R7_q), .clk(Clock));  // open: clr
  assign BusA = decoder_2_out0 ? {16{1'b0}} : 16'bz;  // Controlled_Buffer controlled_buffer_1
  assign BusA = decoder_2_out2 ? R2_q : 16'bz;  // Controlled_Buffer controlled_buffer_2
  assign BusA = decoder_2_out1 ? R1_q : 16'bz;  // Controlled_Buffer controlled_buffer_3
  Decoder #(.select(3)) decoder_2 (
    .out0(decoder_2_out0), .out1(decoder_2_out1), .out2(decoder_2_out2), .out3(decoder_2_out3),
    .out4(decoder_2_out4), .out5(decoder_2_out5), .out6(decoder_2_out6), .out7(decoder_2_out7), .sel(RA),
    .en(1'b1));
  assign BusA = decoder_2_out6 ? R6_q : 16'bz;  // Controlled_Buffer controlled_buffer_4
  assign BusA = decoder_2_out5 ? R5_q : 16'bz;  // Controlled_Buffer controlled_buffer_5
  assign BusA = decoder_2_out4 ? R4_q : 16'bz;  // Controlled_Buffer controlled_buffer_6
  assign BusA = decoder_2_out3 ? R3_q : 16'bz;  // Controlled_Buffer controlled_buffer_7
  assign BusA = decoder_2_out7 ? R7_q : 16'bz;  // Controlled_Buffer controlled_buffer_8
  assign BusB = decoder_3_out0 ? {16{1'b0}} : 16'bz;  // Controlled_Buffer controlled_buffer_9
  assign BusB = decoder_3_out3 ? R3_q : 16'bz;  // Controlled_Buffer controlled_buffer_10
  assign BusB = decoder_3_out2 ? R2_q : 16'bz;  // Controlled_Buffer controlled_buffer_11
  assign BusB = decoder_3_out1 ? R1_q : 16'bz;  // Controlled_Buffer controlled_buffer_12
  Decoder #(.select(3)) decoder_3 (
    .out0(decoder_3_out0), .out1(decoder_3_out1), .out2(decoder_3_out2), .out3(decoder_3_out3),
    .out4(decoder_3_out4), .out5(decoder_3_out5), .out6(decoder_3_out6), .out7(decoder_3_out7), .sel(RB),
    .en(1'b1));
  assign BusB = decoder_3_out7 ? R7_q : 16'bz;  // Controlled_Buffer controlled_buffer_13
  assign BusB = decoder_3_out6 ? R6_q : 16'bz;  // Controlled_Buffer controlled_buffer_14
  assign BusB = decoder_3_out5 ? R5_q : 16'bz;  // Controlled_Buffer controlled_buffer_15
  assign BusB = decoder_3_out4 ? R4_q : 16'bz;  // Controlled_Buffer controlled_buffer_16

  // Notes on the sheet:
  //   STAGE 1
  //   STAGE 2
endmodule

module ALU (
  input  [3:0] Op,
  input  [2:0] func,
  input  [15:0] Rs,
  input  [15:0] Rt,
  output [15:0] Rd
);

  wire comparator_1_eq, comparator_1_gt, comparator_2_eq, comparator_2_gt, comparator_3_eq, not_2_out,
       not_3_out, not_4_out, or_2_out, or_3_out;
  wire [15:0] adder_1_out, adder_2_out, and_1_out, and_2_out, bit_extender_1_out, bit_extender_2_out,
       bit_extender_3_out, bit_extender_4_out, bit_extender_5_out, bit_extender_6_out, bit_extender_7_out,
       bit_extender_8_out, bit_extender_9_out, multiplexer_1_out, multiplexer_2_out, not_1_out, not_5_out,
       or_1_out, shifter_1_out, shifter_2_out, shifter_3_out, shifter_4_out, subtractor_1_out, xor_1_out;

  assign or_1_out = Rs | Rt;  // OR_Gate or_1, 16 bits wide
  assign xor_1_out = Rt ^ Rs;  // XOR_Gate xor_1, 16 bits wide
  assign and_1_out = Rt & Rs;  // AND_Gate and_1, 16 bits wide
  Adder #(.width(16)) adder_1 (.a(Rt), .b(Rs), .out(adder_1_out));  // open: cin, cout
  Subtractor #(.width(16)) subtractor_1 (.a(Rt), .b(Rs), .out(subtractor_1_out));  // open: bin, bout
  Comparator #(.width(16)) comparator_1 (.a(Rt), .b(Rs), .gt(comparator_1_gt), .eq(comparator_1_eq));  // open: lt
  Comparator #(.width(16), .mode("unsigned")) comparator_2 (
    .a(Rt), .b(Rt), .gt(comparator_2_gt), .eq(comparator_2_eq));  // open: lt
  Shifter #(.width(16)) shifter_1 (.in(Rs), .\dist (Rt[3:0]), .out(shifter_1_out));
  Shifter #(.width(16), .shift("ar")) shifter_2 (.in(Rs), .\dist (Rt[3:0]), .out(shifter_2_out));
  Comparator #(.width(16), .mode("unsigned")) comparator_3 (
    .a(Rs), .b({16{1'b0}}), .eq(comparator_3_eq));  // open: gt, lt
  assign not_1_out = ~and_1_out;  // NOT_Gate not_1, 16 bits wide
  or or_2 (or_2_out, comparator_1_gt, comparator_1_eq);
  or or_3 (or_3_out, comparator_2_gt, comparator_2_eq);
  Shifter #(.width(16), .shift("lr")) shifter_3 (.in(Rs), .\dist (Rt[3:0]), .out(shifter_3_out));
  Shifter #(.width(16), .shift("rr")) shifter_4 (.in(Rs), .\dist (Rt[3:0]), .out(shifter_4_out));
  assign bit_extender_1_out = {{15{1'b1}}, comparator_3_eq};  // Bit_Extender bit_extender_1
  assign bit_extender_2_out = {{15{1'b0}}, or_2_out};  // Bit_Extender bit_extender_2
  assign bit_extender_3_out = {{15{1'b0}}, or_3_out};  // Bit_Extender bit_extender_3
  assign and_2_out = bit_extender_1_out & Rt;  // AND_Gate and_2, 16 bits wide
  Multiplexer #(.select(3), .width(16), .enable("false")) multiplexer_1 (
    .in0(or_1_out), .in1(and_1_out), .in2(not_1_out), .in3(xor_1_out), .in4(adder_1_out),
    .in5(subtractor_1_out), .in6(bit_extender_2_out), .in7(bit_extender_3_out), .out(multiplexer_1_out),
    .sel(func));
  not not_2 (not_2_out, comparator_2_eq);
  not not_3 (not_3_out, or_2_out);
  not not_4 (not_4_out, comparator_1_gt);
  Multiplexer #(.select(3), .width(16), .enable("false")) multiplexer_2 (
    .in0(shifter_1_out), .in1(shifter_3_out), .in2(shifter_2_out), .in3(shifter_4_out), .in4(and_2_out),
    .in5(not_5_out), .in6({16{1'b0}}), .in7({16{1'b0}}), .out(multiplexer_2_out), .sel(func));
  assign not_5_out = ~and_2_out;  // NOT_Gate not_5, 16 bits wide
  assign bit_extender_4_out = {{15{1'b0}}, not_2_out};  // Bit_Extender bit_extender_4
  assign bit_extender_5_out = {{15{1'b0}}, comparator_2_eq};  // Bit_Extender bit_extender_5
  assign bit_extender_6_out = {{15{1'b0}}, comparator_1_gt};  // Bit_Extender bit_extender_6
  assign bit_extender_7_out = {{15{1'b0}}, or_2_out};  // Bit_Extender bit_extender_7
  assign bit_extender_8_out = {{15{1'b0}}, not_3_out};  // Bit_Extender bit_extender_8
  assign bit_extender_9_out = {{15{1'b0}}, not_4_out};  // Bit_Extender bit_extender_9
  Adder #(.width(16)) adder_2 (.a(Rs), .b(Rt), .out(adder_2_out));  // open: cin, cout
  Multiplexer #(.select(4), .width(16), .enable("false")) multiplexer_3 (
    .in0(multiplexer_1_out), .in1(multiplexer_2_out), .in2(and_1_out), .in3(or_1_out), .in4(adder_1_out),
    .in5(adder_2_out), .in6(adder_2_out), .in7(bit_extender_4_out), .in8(bit_extender_5_out),
    .in9(bit_extender_6_out), .in10(bit_extender_7_out), .in11(bit_extender_8_out),
    .in12(bit_extender_9_out), .in13({16{1'b0}}), .in14({16{1'b0}}), .in15({16{1'b0}}), .out(Rd), .sel(Op));

  // Notes on the sheet:
  //   ALU For Op = 0000
  //   OR 
  //   NAND
  //   XOR
  //   ADD
  //   SUB
  //   SGE
  //   SGEU
  //   ALU For Op = 0001
  //   SLL
  //   SRL
  //   SRA
  //   ROR
  //   MOVZ MOVN
  //   Signed
endmodule
